# Fritzing sketch esp8266_bmp180_server (saved by Fritzing 0.9.3b)

parts:
  Part1 = Adafruit HUZZAH ESP8266 [part_number="Adafruit #2471"]
  Part2 = Adafruit BMP180

nets:
  VIN: Part1.VIN, Part2.+5V
  GND: Part1.GND, Part2.GND
  N1: Part1.GPIO4, Part2.SDA
  N2: Part1.GPIO5, Part2.SCL

notes:
  USB +
  USB -

custom parts:
  Adafruit HUZZAH ESP8266: Add Internet to your next project with an adorable, bite-sized WiFi microcontroller, at a price you like! The ESP8266 processor from Espressif is an 80 MHz microcontroller with a full WiFi front-end (both as client and access point) and TCP/IP stack with DNS support as well. While this chip has been very popular, its also been very difficult to use. Most of the low cost modules are not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
  Adafruit BMP180: This precision sensor from Bosch is the best low-cost sensing solution for measuring barometric pressure and temperature. Because pressure changes with altitude you can also use it as an altimeter! The sensor is soldered onto a PCB with a 3.3V regulator, I2C level shifter and pull-up resistors on the I2C pins. The BMP180 is the next-generation of sensors from Bosch, and replaces the BMP085.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
